// Logisim project CPU.circ as structural Verilog: 6 circuits, main circuit main
module main (
  input  CLR,
  input  in_2,
  output [15:0] out_3,
  output [15:0] out_4,
  output [15:0] out_5,
  output [15:0] out_6,
  output [15:0] out_7
);

  wire ALUsrc, clk, Dsrc, flgW, memW, PC_W, PCregIn, Rwrite, undriven;
  wire [1:0] alu_1_zero, flags;
  wire [2:0] ALUop, Ra, Rb, Rdest;
  wire [15:0] AUIPC, imm, multiplexer_1_out, multiplexer_2_out, PC, regfile_1_b, rom_1_data;

  Adder #(.width(16)) adder_1 (.a(PC), .b(imm), .out(AUIPC));  // open: cin, cout
  Counter #(.max('hffff), .width(16)) counter_1 (
    .load(PC_W), .D(AUIPC), .count(undriven), .Q(PC), .clk(clk), .clr(in_2));  // open: carry, up
  ROM #(.addrWidth(16), .dataWidth(16)) rom_1 (.addr(PC), .data(rom_1_data));
  RAM #(.addrWidth(16), .dataWidth(16), .enables("line")) ram_1 (
    .addr(out_7), .we(memW), .clk(clk), .din(out_4), .dout(out_3));
  Multiplexer #(.width(16)) multiplexer_1 (.in0(out_7), .in1(out_3), .out(multiplexer_1_out), .sel(Dsrc));
  Multiplexer #(.width(16)) multiplexer_2 (
    .in0(multiplexer_1_out), .in1(AUIPC), .out(multiplexer_2_out), .sel(PCregIn));
  controlUnit controlunit_1 (
    .Instr(rom_1_data), .flags(flags), .Rdest(Rdest), .Ra(Ra), .Rb(Rb), .Rwrite(Rwrite), .ALUop(ALUop),
    .ALUimmSrc(ALUsrc), .Immidiate(imm), .MemW(memW), .dataSrc(Dsrc), .flagWrite(flgW), .PCwrite(PC_W),
    .PCin(PCregIn));
  RegFile regfile_1 (
    .W_addr(Rdest), .A_addr(Ra), .B_addr(Rb), .Data(multiplexer_2_out), .W(Rwrite), .CLK(clk), .in_7(CLR),
    .A(out_5), .B(regfile_1_b), .C(out_4));
  Multiplexer #(.width(16)) multiplexer_3 (.in0(regfile_1_b), .in1(imm), .out(out_6), .sel(ALUsrc));
  Clock clock_1 (.out(clk));
  ALU alu_1 (.in_1(out_5), .in_2(out_6), .in_3(ALUop), .out_4(out_7), .zero(alu_1_zero[0]), .neg(alu_1_zero[1]));
  Register #(.width(2)) u_flags (.D(alu_1_zero), .en(flgW), .Q(flags), .clk(clk), .clr(CLR));

  // Other names for the same wires on the sheet: mem[15:0] = out_3; mem_D[15:0] = out_4; res[15:0] = out_7

  // Notes on the sheet:
  //   contents of rom_1 (hex, n*v repeats v):
  //   481 2901 180 2810 323 c92 481 581 10 fd03
endmodule

module ALU (
  input  [15:0] in_1,
  input  [15:0] in_2,
  input  [2:0] in_3,
  output [15:0] out_4,
  output zero,
  output neg
);

  wire [15:0] adder_1_out, and_1_out, or_1_out, shifter_1_out, shifter_2_out, shifter_3_out,
       subtractor_1_out, xor_1_out;

  Adder #(.width(16)) adder_1 (.a(in_1), .b(in_2), .out(adder_1_out));  // open: cin, cout
  Subtractor #(.width(16)) subtractor_1 (.a(in_1), .b(in_2), .out(subtractor_1_out));  // open: bin, bout
  assign and_1_out = in_1 & in_2;  // AND_Gate and_1, 16 bits wide
  assign or_1_out = in_1 | in_2;  // OR_Gate or_1, 16 bits wide
  assign xor_1_out = in_1 ^ in_2;  // XOR_Gate xor_1, 16 bits wide
  Shifter #(.width(16)) shifter_1 (.in(in_1), .\dist (in_2[3:0]), .out(shifter_1_out));
  Shifter #(.shift("lr"), .width(16)) shifter_2 (.in(in_1), .\dist (in_2[3:0]), .out(shifter_2_out));
  Shifter #(.shift("ar"), .width(16)) shifter_3 (.in(in_1), .\dist (in_2[3:0]), .out(shifter_3_out));
  Multiplexer #(.select(3), .width(16)) multiplexer_1 (
    .in0(adder_1_out), .in1(subtractor_1_out), .in2(and_1_out), .in3(or_1_out), .in4(xor_1_out),
    .in5(shifter_1_out), .in6(shifter_2_out), .in7(shifter_3_out), .out(out_4), .sel(in_3));
  Comparator #(.width(16)) comparator_1 (.a(out_4), .b({16{1'b0}}), .eq(zero), .lt(neg));  // open: gt
endmodule

module controlUnit (
  input  [15:0] Instr,
  input  [1:0] flags,
  output [2:0] Rdest,
  output [2:0] Ra,
  output [2:0] Rb,
  output Rwrite,
  output [2:0] ALUop,
  output ALUimmSrc,
  output [15:0] Immidiate,
  output MemW,
  output dataSrc,
  output flagWrite,
  output PCwrite,
  output PCin
);

  wire B, B0, M, multiplexer_1_out, nor_1_out, not_1_out, not_2_out, not_3_out, not_4_out, not_5_out, R;
  wire [15:0] imm, Limm;

  Decoder #(.enable("false"), .select(4)) decoder_1 (
    .out0(R), .out1(ALUimmSrc), .out2(M), .out3(B), .sel(Instr[3:0]));  // open: out4, out5, out6, out7, out8, out9, out10, out11, out12, out13, out14, out15
  and and_1 (B0, B, not_1_out);
  not not_1 (not_1_out, Instr[6]);
  and and_2 (PCin, B, Instr[6]);
  completer completer_1 (.in_1(Instr[15:10]), .out_2(imm));
  completer9 completer9_1 (.in_1(Instr[15:7]), .out_2(Limm));
  not not_2 (not_2_out, flags[0]);
  nor nor_1 (nor_1_out, flags[0], flags[1]);
  not not_3 (not_3_out, Instr[4]);
  Multiplexer #(.select(2)) multiplexer_1 (
    .in0(flags[0]), .in1(not_2_out), .in2(flags[1]), .in3(nor_1_out), .out(multiplexer_1_out),
    .sel(Instr[5:4]));
  Multiplexer #(.width(3)) multiplexer_2 (.in0(Instr[12:10]), .in1(Instr[9:7]), .out(Ra), .sel(ALUimmSrc));
  not not_4 (not_4_out, MemW);
  not not_5 (not_5_out, B0);
  Multiplexer #(.width(3)) multiplexer_3 (.in0(Instr[6:4]), .in1(3'b000), .out(ALUop), .sel(M));
  Multiplexer #(.width(16)) multiplexer_4 (.in0(imm), .in1(Limm), .out(Immidiate), .sel(B0));
  and and_3 (MemW, M, Instr[4]);
  and and_4 (dataSrc, M, not_3_out);
  or or_1 (flagWrite, R, ALUimmSrc);
  and and_5 (PCwrite, B0, multiplexer_1_out);
  and and_6 (Rwrite, not_4_out, not_5_out);

  assign Rb = Instr[15:13];
  assign Rdest = Instr[9:7];

  // Other names for the same wires on the sheet: B1 = PCin; I = ALUimmSrc; op[3:0] = Instr[3:0];
  //   func[2:0] = Instr[6:4]; Rd[2:0] = Instr[9:7]; Ra_t[2:0] = Instr[12:10]
endmodule

module RegFile (
  input  [2:0] W_addr,
  input  [2:0] A_addr,
  input  [2:0] B_addr,
  input  [15:0] Data,
  input  W,
  input  CLK,
  input  in_7,
  output [15:0] A,
  output [15:0] B,
  output [15:0] C
);

  wire demultiplexer_1_out1, demultiplexer_1_out2, demultiplexer_1_out3, demultiplexer_1_out4,
       demultiplexer_1_out5, demultiplexer_1_out6, demultiplexer_1_out7;
  wire [15:0] register_1_q, register_2_q, register_3_q, register_4_q, register_5_q, register_6_q,
       register_7_q;

  Demultiplexer #(.select(3)) demultiplexer_1 (
    .out1(demultiplexer_1_out1), .out2(demultiplexer_1_out2), .out3(demultiplexer_1_out3),
    .out4(demultiplexer_1_out4), .out5(demultiplexer_1_out5), .out6(demultiplexer_1_out6),
    .out7(demultiplexer_1_out7), .in(W), .sel(W_addr));  // open: out0
  Register #(.width(16)) register_1 (.D(Data), .en(demultiplexer_1_out1), .clk(CLK), .Q(register_1_q), .clr(in_7));
  Register #(.width(16)) register_2 (.D(Data), .en(demultiplexer_1_out2), .clk(CLK), .Q(register_2_q), .clr(in_7));
  Register #(.width(16)) register_3 (.D(Data), .en(demultiplexer_1_out3), .clk(CLK), .Q(register_3_q), .clr(in_7));
  Register #(.width(16)) register_4 (.D(Data), .en(demultiplexer_1_out4), .clk(CLK), .Q(register_4_q), .clr(in_7));
  Register #(.width(16)) register_5 (.D(Data), .en(demultiplexer_1_out5), .clk(CLK), .Q(register_5_q), .clr(in_7));
  Register #(.width(16)) register_6 (.D(Data), .en(demultiplexer_1_out6), .clk(CLK), .Q(register_6_q), .clr(in_7));
  Register #(.width(16)) register_7 (.D(Data), .en(demultiplexer_1_out7), .clk(CLK), .Q(register_7_q), .clr(in_7));
  Multiplexer #(.select(3), .width(16)) multiplexer_1 (
    .in0({16{1'b0}}), .in1(register_1_q), .in2(register_2_q), .in3(register_3_q), .in4(register_4_q),
    .in5(register_5_q), .in6(register_6_q), .in7(register_7_q), .out(A), .sel(A_addr));
  Multiplexer #(.select(3), .width(16)) multiplexer_2 (
    .in0({16{1'b0}}), .in1(register_1_q), .in2(register_2_q), .in3(register_3_q), .in4(register_4_q),
    .in5(register_5_q), .in6(register_6_q), .in7(register_7_q), .out(B), .sel(B_addr));
  Multiplexer #(.select(3), .width(16)) multiplexer_3 (
    .in0({16{1'b0}}), .in1(register_1_q), .in2(register_2_q), .in3(register_3_q), .in4(register_4_q),
    .in5(register_5_q), .in6(register_6_q), .in7(register_7_q), .out(C), .sel(W_addr));

  // Other names for the same wires on the sheet: Waddr[2:0] = W_addr
endmodule

module completer (
  input  [5:0] in_1,
  output [15:0] out_2
);


  assign out_2 = {{11{in_1[5]}}, in_1[4:0]};
endmodule

module completer9 (
  input  [8:0] in_1,
  output [15:0] out_2
);


  assign out_2 = {{8{in_1[8]}}, in_1[7:0]};
endmodule
